# Fritzing sketch schematics (saved by Fritzing 0.9.9b)

parts:
  MCU1 = Raspberry Pi Zero
  Part1 = Adafruit ADS1115 16Bit I2C ADC [part_number="Adafruit #1085"]
  R1 = Resistor [tolerance=±5% resistance=100 package="2010 [SMD]"]

nets:
  N1: MCU1.pin_1, Part1.VDD
  N2: MCU1.pin_3, Part1.SDA
  N3: MCU1.pin_5, Part1.SCL
  N4: MCU1.pin_6, MCU1.pin_9, Part1.GND
  N5: Part1.AIN1, R1.Pin_1
  N6: Part1.AIN0, R1.Pin_0

custom parts:
  Adafruit ADS1115 16Bit I2C ADC: For microcontrollers without an analog-to-digital converter or when you want a higher-precision ADC, the ADS1115 provides 16-bit precision at 860 samples/second over I2C. The chip can be configured as 4 single-ended input channels, or two differential channels. As a nice bonus, it even includes a programmable gain amplifier, up to x16, to help boost up smaller single/differential signals to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
